# Fritzing sketch exemplo-05-sala (saved by Fritzing 0.9.1b)
breadboards: 1

parts:
  Componente1 = Arduino Uno (Rev3)
  LDR1 = Photocell (LDR) [package=THT]
  R3 = Resistor [tolerance=±5% resistance=220 package=THT]
  R4 = Resistor [tolerance=±5% resistance=220 package=THT]
  LED2 = smd LED [color="Red (633nm)" package="0603 [SMD]"]
  U1 = POT [package=pot_mammoth]
  LCD1 = LCD screen

nets:
  N1: Componente1.A0, LDR1.pin_1, R3.Pin_0
  N2: Componente1.D11_PWM/MOSI, LCD1.E
  N3: Componente1.D12/MISO, LCD1.RS
  N4: Componente1.D13/SCK, R4.Pin_1
  GND: Componente1.GND, R3.Pin_1, LED2.cathode, U1.E, LCD1.VSS, LCD1.R/W, LCD1.LED-
  N5: Componente1.D2, LCD1.DB7
  N6: Componente1.D3_PWM, LCD1.DB6
  N7: Componente1.D4, LCD1.DB5
  N8: Componente1.D5_PWM, LCD1.DB4
  5V: Componente1.5V, LDR1.pin_0, U1.S, LCD1.VDD, LCD1.LED+
  N9: R4.Pin_0, LED2.anode
  N10: U1.A, LCD1.V0
